# Fritzing sketch gateway (saved by Fritzing 0.9.3b)

parts:
  U2 = NodeMCU V3.0
  Part1 = NRF24L01+ Breakout Board
  Factory_reset = Pushbutton [package="[THT]"]

nets:
  N1: U2.D2, Part1.CS
  N2: U2.D4, Part1.CE
  3V3: U2.3V3, Part1.VCC
  N3: U2.D5, Part1.SCK
  N4: U2.D6, Part1.MISO
  N5: U2.D7, Part1.MOSI
  N6: U2.RX, Factory_reset.Pin_4
  GND: U2.GND, Part1.GND, Factory_reset.Pin_1, Factory_reset.Pin_2

custom parts:
  NodeMCU V3.0: ESP8266 based NodeMCU
