# Fritzing sketch node01 (saved by Fritzing 0.9.3b)
circuit board: 8.46667cm x 5.64444cm

parts:
  Part1 = Arduino Nano (Rev3.0) (ICSP)
  Part2 = NRF24L01+ Breakout Board
  M1 = Humidity and Temperature Sensor DHT11

nets:
  GND: Part1.GND, Part2.GND, M1.GND
  N1: Part1.D3, M1.Data
  N2: Part1.D9, Part2.CE
  N3: Part1.D10, Part2.CS
  N4: Part1.D11/MOSI, Part2.MOSI
  N5: Part1.D12/MISO, Part2.MISO
  5V: Part1.5V, M1.Vcc
  3V3: Part1.3V3, Part2.VCC
  N6: Part1.D13/SCK, Part2.SCK

custom parts:
  Humidity and Temperature Sensor DHT11: Digital relative humidity & temperature sensor DHT11
